# Fritzing sketch arduino (saved by Fritzing 0.9.2b)
breadboards: 1

parts:
  Part4 = Arduino Uno (Rev3)
  R6 = Resistor [tolerance=±5% resistance=220 package="0402 [SMD]"]
  R7 = Resistor [tolerance=±5% resistance=220 package="0402 [SMD]"]
  R8 = Resistor [tolerance=±5% resistance=220 package="0402 [SMD]"]
  R9 = Resistor [tolerance=±5% resistance=220 package="0402 [SMD]"]
  S2 = SWITCH-MOMENTARY-2 [package=tactile-pth-12mm]
  S3 = SWITCH-MOMENTARY-2 [package=tactile-pth-12mm]
  S4 = SWITCH-MOMENTARY-2 [package=tactile-pth-12mm]
  S5 = SWITCH-MOMENTARY-2 [package=tactile-pth-12mm]
  LED11 = LED - 5mm [color="Green (555nm)" package="5 mm [THT]"]
  LED12 = LED - 5mm [color="Yellow (585nm)" package="5 mm [THT]"]
  LED13 = LED - 5mm [color="Red (633nm)" package="5 mm [THT]"]
  LED14 = LED - 5mm [color="Blue (430nm)" package="5 mm [THT]"]
  J1 = Piezo Speaker

nets:
  N1: Part4.D8, J1.pin2
  N2: Part4.D9_PWM, LED11.anode
  N3: Part4.D10_PWM/SS, LED12.anode
  N4: Part4.D11_PWM/MOSI, LED13.anode
  N5: Part4.D12/MISO, LED14.anode
  N6: Part4.GND, R6.Pin_0, R7.Pin_0, R8.Pin_0, R9.Pin_0, S2.pin_3, S3.pin_3, S4.pin_3, S5.pin_3, J1.pin1
  N7: Part4.D2, S5.2
  N8: Part4.D3_PWM, S4.2
  N9: Part4.D4, S3.2
  N10: Part4.D5_PWM, S2.2
  N11: R6.Pin_1, LED11.cathode
  N12: R7.Pin_1, LED12.cathode
  N13: R8.Pin_1, LED13.cathode
  N14: R9.Pin_1, LED14.cathode

custom parts:
  SWITCH-MOMENTARY-2: Various NO switches- pushbuttons, reed, etc
